// Logisim project cpu8.circ as structural Verilog: 17 circuits, main circuit AND_8_bits
module AND_8_bits (
  input  [7:0] in_1,
  input  [7:0] in_2,
  output [7:0] out_3
);

  and and_1 (out_3[0], in_1[0], in_2[0]);
  and and_2 (out_3[1], in_1[1], in_2[1]);
  and and_3 (out_3[2], in_1[2], in_2[2]);
  and and_4 (out_3[3], in_1[3], in_2[3]);
  and and_5 (out_3[4], in_1[4], in_2[4]);
  and and_6 (out_3[5], in_1[5], in_2[5]);
  and and_7 (out_3[6], in_1[6], in_2[6]);
  and and_8 (out_3[7], in_1[7], in_2[7]);
endmodule

module UL_step_2 (
  input  [7:0] A,
  input  [7:0] B,
  output [7:0] out_3,
  output [7:0] out_4,
  output [7:0] out_5
);

  AND_8_bits and_8_bits_1 (.in_1(A), .in_2(B), .out_3(out_3));
  OR_8_bits or_8_bits_1 (.in_1(A), .in_2(B), .out_3(out_4));
  XOR_8_bits xor_8_bits_1 (.in_1(A), .in_2(B), .out_3(out_5));
endmodule

module OR_8_bits (
  input  [7:0] in_1,
  input  [7:0] in_2,
  output [7:0] out_3
);

  or or_1 (out_3[0], in_1[0], in_2[0]);
  or or_2 (out_3[1], in_1[1], in_2[1]);
  or or_3 (out_3[2], in_1[2], in_2[2]);
  or or_4 (out_3[3], in_1[3], in_2[3]);
  or or_5 (out_3[4], in_1[4], in_2[4]);
  or or_6 (out_3[5], in_1[5], in_2[5]);
  or or_7 (out_3[6], in_1[6], in_2[6]);
  or or_8 (out_3[7], in_1[7], in_2[7]);
endmodule

module XOR_8_bits (
  input  [7:0] in_1,
  input  [7:0] in_2,
  output [7:0] out_3
);

  xor xor_1 (out_3[0], in_1[0], in_2[0]);
  xor xor_2 (out_3[1], in_1[1], in_2[1]);
  xor xor_3 (out_3[2], in_1[2], in_2[2]);
  xor xor_4 (out_3[3], in_1[3], in_2[3]);
  xor xor_5 (out_3[4], in_1[4], in_2[4]);
  xor xor_6 (out_3[5], in_1[5], in_2[5]);
  xor xor_7 (out_3[6], in_1[6], in_2[6]);
  xor xor_8 (out_3[7], in_1[7], in_2[7]);
endmodule

module ADDITIONEUR_1_bit (
  input  A,
  input  B,
  input  RETENUE_IN,
  output RETENUE_OUT,
  output S
);

  wire ADDITION_bit_out, not_1_out, not_2_out, not_3_out, not_4_out, RETENUE_1_out, RETENUE_2_out, xor_1_out,
       xor_2_out, xor_3_out, xor_4_out;

  not not_1 (not_1_out, A);
  not not_2 (not_2_out, B);
  and RETENUE_1 (RETENUE_1_out, A, B);
  xor xor_1 (xor_1_out, B, A);
  xor xor_2 (xor_2_out, not_1_out, not_2_out);
  and ADDITION_bit (ADDITION_bit_out, xor_1_out, xor_2_out);
  not not_3 (not_3_out, ADDITION_bit_out);
  not not_4 (not_4_out, RETENUE_IN);
  and RETENUE_2 (RETENUE_2_out, ADDITION_bit_out, RETENUE_IN);
  xor xor_3 (xor_3_out, RETENUE_IN, ADDITION_bit_out);
  xor xor_4 (xor_4_out, not_3_out, not_4_out);
  or or_1 (RETENUE_OUT, RETENUE_1_out, RETENUE_2_out);
  and ADDITION_bit_RETENUE (S, xor_3_out, xor_4_out);
endmodule

module ADDITIONEUR_8_bits (
  input  [7:0] A,
  input  [7:0] B,
  input  RESTE,
  output [7:0] Somme,
  output RETENUE_OUT
);

  wire additioneur_1_bit_1_retenue_out, additioneur_1_bit_2_retenue_out, additioneur_1_bit_3_retenue_out,
       additioneur_1_bit_4_retenue_out, additioneur_1_bit_5_retenue_out, additioneur_1_bit_6_retenue_out,
       additioneur_1_bit_7_retenue_out;

  ADDITIONEUR_1_bit additioneur_1_bit_1 (
    .A(A[0]), .B(B[0]), .RETENUE_IN(RESTE), .RETENUE_OUT(additioneur_1_bit_1_retenue_out), .S(Somme[0]));
  ADDITIONEUR_1_bit additioneur_1_bit_2 (
    .A(A[1]), .B(B[1]), .RETENUE_IN(additioneur_1_bit_1_retenue_out),
    .RETENUE_OUT(additioneur_1_bit_2_retenue_out), .S(Somme[1]));
  ADDITIONEUR_1_bit additioneur_1_bit_3 (
    .A(A[2]), .B(B[2]), .RETENUE_IN(additioneur_1_bit_2_retenue_out),
    .RETENUE_OUT(additioneur_1_bit_3_retenue_out), .S(Somme[2]));
  ADDITIONEUR_1_bit additioneur_1_bit_4 (
    .A(A[3]), .B(B[3]), .RETENUE_IN(additioneur_1_bit_3_retenue_out),
    .RETENUE_OUT(additioneur_1_bit_4_retenue_out), .S(Somme[3]));
  ADDITIONEUR_1_bit additioneur_1_bit_5 (
    .A(A[4]), .B(B[4]), .RETENUE_IN(additioneur_1_bit_4_retenue_out),
    .RETENUE_OUT(additioneur_1_bit_5_retenue_out), .S(Somme[4]));
  ADDITIONEUR_1_bit additioneur_1_bit_6 (
    .A(A[5]), .B(B[5]), .RETENUE_IN(additioneur_1_bit_5_retenue_out),
    .RETENUE_OUT(additioneur_1_bit_6_retenue_out), .S(Somme[5]));
  ADDITIONEUR_1_bit additioneur_1_bit_7 (
    .A(A[6]), .B(B[6]), .RETENUE_IN(additioneur_1_bit_6_retenue_out),
    .RETENUE_OUT(additioneur_1_bit_7_retenue_out), .S(Somme[6]));
  ADDITIONEUR_1_bit additioneur_1_bit_8 (
    .A(A[7]), .B(B[7]), .RETENUE_IN(additioneur_1_bit_7_retenue_out), .RETENUE_OUT(RETENUE_OUT), .S(Somme[7]));
endmodule

module UAL_8_BITS (
  input  [7:0] A,
  input  [7:0] B,
  input  RESTE,
  input  [1:0] SELECTIONNEUR_ADD_AND_OR_XOR,
  output [7:0] S
);

  wire [7:0] additioneur_8_bits_1_somme, ul_step_2_1_out_3, ul_step_2_1_out_4, ul_step_2_1_out_5;

  ADDITIONEUR_8_bits additioneur_8_bits_1 (
    .A(A), .B(B), .RESTE(RESTE), .Somme(additioneur_8_bits_1_somme));  // open: RETENUE_OUT
  UL_step_2 ul_step_2_1 (.A(A), .B(B), .out_3(ul_step_2_1_out_3), .out_4(ul_step_2_1_out_4), .out_5(ul_step_2_1_out_5));
  Multiplexer #(.select(2), .width(8)) multiplexer_1 (
    .in0(additioneur_8_bits_1_somme), .in1(ul_step_2_1_out_3), .in2(ul_step_2_1_out_4),
    .in3(ul_step_2_1_out_5), .out(S), .sel(SELECTIONNEUR_ADD_AND_OR_XOR));
endmodule

module REGISTRE_8_bits (
  input  [7:0] DONNEES,
  input  WE,
  input  CLOCK,
  input  RESET,
  output [7:0] FORMER_DATA
);

  Register #(.width(1)) register_1 (.D(DONNEES[0]), .en(WE), .clk(CLOCK), .Q(FORMER_DATA[0]), .clr(RESET));
  Register #(.width(1)) register_2 (.D(DONNEES[1]), .en(WE), .clk(CLOCK), .Q(FORMER_DATA[1]), .clr(RESET));
  Register #(.width(1)) register_3 (.D(DONNEES[2]), .en(WE), .clk(CLOCK), .Q(FORMER_DATA[2]), .clr(RESET));
  Register #(.width(1)) register_4 (.D(DONNEES[3]), .en(WE), .clk(CLOCK), .Q(FORMER_DATA[3]), .clr(RESET));
  Register #(.width(1)) register_5 (.D(DONNEES[4]), .en(WE), .clk(CLOCK), .Q(FORMER_DATA[4]), .clr(RESET));
  Register #(.width(1)) register_6 (.D(DONNEES[5]), .en(WE), .clk(CLOCK), .Q(FORMER_DATA[5]), .clr(RESET));
  Register #(.width(1)) register_7 (.D(DONNEES[6]), .en(WE), .clk(CLOCK), .Q(FORMER_DATA[6]), .clr(RESET));
  Register #(.width(1)) register_8 (.D(DONNEES[7]), .en(WE), .clk(CLOCK), .Q(FORMER_DATA[7]), .clr(RESET));
endmodule

module BANC_4_REGISTRES (
  input  [7:0] DATA_TO_STORE,
  input  [1:0] STORE_IN_REGISTRER,
  input  WE,
  input  CLOCK,
  input  [1:0] LOAD_ON_OUTPUT_A_FROM_REGISTRER,
  input  RESET,
  input  [1:0] LOAD_ON_OUTPUT_B_FROM_REGISTRER,
  output [7:0] A,
  output [7:0] B
);

  wire [7:0] multiplexer_1_out, multiplexer_2_out, multiplexer_3_out, multiplexer_4_out,
       REGISTRE_0_former_data, REGISTRE_1_former_data, REGISTRE_2_former_data, REGISTRE_3_former_data;

  Multiplexer #(.select(2), .width(8)) multiplexer_1 (
    .in0(DATA_TO_STORE), .in1(REGISTRE_0_former_data), .in2(REGISTRE_0_former_data),
    .in3(REGISTRE_0_former_data), .out(multiplexer_1_out), .sel(STORE_IN_REGISTRER));
  Multiplexer #(.select(2), .width(8)) multiplexer_2 (
    .in0(REGISTRE_1_former_data), .in1(DATA_TO_STORE), .in2(REGISTRE_1_former_data),
    .in3(REGISTRE_1_former_data), .out(multiplexer_2_out), .sel(STORE_IN_REGISTRER));
  Multiplexer #(.select(2), .width(8)) multiplexer_3 (
    .in0(REGISTRE_2_former_data), .in1(REGISTRE_2_former_data), .in2(DATA_TO_STORE),
    .in3(REGISTRE_2_former_data), .out(multiplexer_3_out), .sel(STORE_IN_REGISTRER));
  Multiplexer #(.select(2), .width(8)) multiplexer_4 (
    .in0(REGISTRE_3_former_data), .in1(REGISTRE_3_former_data), .in2(REGISTRE_3_former_data),
    .in3(DATA_TO_STORE), .out(multiplexer_4_out), .sel(STORE_IN_REGISTRER));
  REGISTRE_8_bits REGISTRE_0 (
    .DONNEES(multiplexer_1_out), .WE(WE), .CLOCK(CLOCK), .RESET(RESET), .FORMER_DATA(REGISTRE_0_former_data));
  REGISTRE_8_bits REGISTRE_1 (
    .DONNEES(multiplexer_2_out), .WE(WE), .CLOCK(CLOCK), .RESET(RESET), .FORMER_DATA(REGISTRE_1_former_data));
  REGISTRE_8_bits REGISTRE_2 (
    .DONNEES(multiplexer_3_out), .WE(WE), .CLOCK(CLOCK), .RESET(RESET), .FORMER_DATA(REGISTRE_2_former_data));
  REGISTRE_8_bits REGISTRE_3 (
    .DONNEES(multiplexer_4_out), .WE(WE), .CLOCK(CLOCK), .RESET(RESET), .FORMER_DATA(REGISTRE_3_former_data));
  Multiplexer #(.select(2), .width(8)) multiplexer_5 (
    .in0(REGISTRE_0_former_data), .in1(REGISTRE_1_former_data), .in2(REGISTRE_2_former_data),
    .in3(REGISTRE_3_former_data), .out(A), .sel(LOAD_ON_OUTPUT_A_FROM_REGISTRER));
  Multiplexer #(.select(2), .width(8)) multiplexer_6 (
    .in0(REGISTRE_0_former_data), .in1(REGISTRE_1_former_data), .in2(REGISTRE_2_former_data),
    .in3(REGISTRE_3_former_data), .out(B), .sel(LOAD_ON_OUTPUT_B_FROM_REGISTRER));
endmodule

module UAL_ET_BANC (
  input  [1:0] STORING_REGISTER,
  input  WE,
  input  RESTE,
  input  CLOCK,
  input  [1:0] OPERATION,
  input  [1:0] LOAD_A_IN,
  input  RESET,
  input  [1:0] LOAD_B_IN,
  input  [7:0] DATA,
  input  WRITE_RESULT0_OR_DATA1,
  output [7:0] A,
  output [7:0] B
);

  wire [7:0] multiplexer_1_out, ual_8_bits_1_s;

  BANC_4_REGISTRES banc_4_registres_1 (
    .DATA_TO_STORE(multiplexer_1_out), .STORE_IN_REGISTRER(STORING_REGISTER), .WE(WE), .CLOCK(CLOCK),
    .LOAD_ON_OUTPUT_A_FROM_REGISTRER(LOAD_A_IN), .RESET(RESET), .LOAD_ON_OUTPUT_B_FROM_REGISTRER(LOAD_B_IN),
    .A(A), .B(B));
  Multiplexer #(.width(8)) multiplexer_1 (
    .in0(ual_8_bits_1_s), .in1(DATA), .out(multiplexer_1_out), .sel(WRITE_RESULT0_OR_DATA1));
  UAL_8_BITS ual_8_bits_1 (.A(A), .B(B), .RESTE(RESTE), .SELECTIONNEUR_ADD_AND_OR_XOR(OPERATION), .S(ual_8_bits_1_s));
endmodule

module ETAPE7_ROM (
  input  RESET_LOCAL_VARIABLE,
  input  WE,
  input  CLOCK,
  input  RESET_POINTEUR_PROGRAMME,
  output [1:0] out_5,
  output [1:0] out_6,
  output [1:0] out_7,
  output [1:0] out_8,
  output [1:0] out_9,
  output [7:0] VALUE_OPERANDE2,
  output [7:0] VALUE_OPERANDE1,
  output [7:0] out_12,
  output [1:0] out_13,
  output [1:0] out_14,
  output [7:0] out_15,
  output out_16
);

  wire and_1_out;
  wire [7:0] pointeur_programme_1_curr_adress;
  wire [12:0] rom_1_data;

  Pointeur_Programme pointeur_programme_1 (
    .WE(WE), .CLOCK(CLOCK), .RESET(RESET_POINTEUR_PROGRAMME), .CURR_ADRESS(pointeur_programme_1_curr_adress));
  ROM #(.dataWidth(14)) rom_1 (
    .addr(pointeur_programme_1_curr_adress),
    .data({out_16, rom_1_data[12:11], out_14, out_9, out_7, out_6, out_5, rom_1_data[0]}));
  and and_1 (and_1_out, rom_1_data[0], WE);
  Multiplexer #(.width(2)) multiplexer_1 (.in0(out_7), .in1(out_14), .out(out_13), .sel(out_16));
  Multiplexer #(.width(2)) multiplexer_2 (.in0(out_5), .in1(out_14), .out(out_8), .sel(out_16));
  UAL_ET_BANC ual_et_banc_1 (
    .STORING_REGISTER(out_14), .WE(and_1_out), .RESTE(1'b0), .CLOCK(CLOCK), .OPERATION(rom_1_data[12:11]),
    .LOAD_A_IN(out_8), .RESET(RESET_LOCAL_VARIABLE), .LOAD_B_IN(out_13), .DATA({out_9, out_7, out_6, out_5}),
    .WRITE_RESULT0_OR_DATA1(out_16), .A(VALUE_OPERANDE2), .B(VALUE_OPERANDE1));

  assign out_12 = {out_9, out_7, out_6, out_5};
  assign out_15 = {out_9, out_7, out_6, out_5};

  // Notes on the sheet:
  //   ENCODAGE INSTRUCTION
  //   xx xx xx xx
  //   Les opérations sont encodées de 0à 3 : ADD (0) AND (1) OR (2) XOR (3)
  //   sous la forme operation resultat operande1 operande2
  //   Les opérandes et le résultat représente le numéro du registre dans lequel ils sont stocké (0-3)
  //   2 bits pour l'opération | 2 bits pour le numéro du registre (opérande et résultat) | 4 bits pour le WE des 4 registres
  //   contents of rom_1 (hex, n*v repeats v):
  //   220b 421 1e25 847 1205
endmodule

module Pointeur_Programme (
  input  WE,
  input  CLOCK,
  input  RESET,
  output [7:0] CURR_ADRESS
);

  wire additioneur_8_bits_1_retenue_out;
  wire [7:0] additioneur_8_bits_1_somme;

  ADDITIONEUR_8_bits additioneur_8_bits_1 (
    .A(CURR_ADRESS), .B(8'h1), .RESTE(additioneur_8_bits_1_retenue_out), .Somme(additioneur_8_bits_1_somme),
    .RETENUE_OUT(additioneur_8_bits_1_retenue_out));
  REGISTRE_8_bits registre_8_bits_1 (
    .DONNEES(additioneur_8_bits_1_somme), .WE(WE), .CLOCK(CLOCK), .RESET(RESET), .FORMER_DATA(CURR_ADRESS));
endmodule

module ETAPE8_RAM (
  input  WE,
  input  CLOCK,
  input  RESET_REGISTRES,
  input  RESET_POINTEUR_PROGRAMME,
  output [7:0] OPERANDE1,
  output [7:0] OPERANDE2,
  output [7:0] out_7
);

  wire decodage_instruction_1_load_immediat, decodage_instruction_1_load_ram,
       decodage_instruction_1_ram_read, decodage_instruction_1_ram_write,
       decodage_instruction_1_registre_operation_data, decodage_instruction_1_we;
  wire [1:0] decodage_instruction_1_a_addr_registre_result, decodage_instruction_1_b_addr_registre_operande1,
       decodage_instruction_1_c_addr_registre_operande2, decodage_instruction_1_d_addr_registre_src_stock,
       decodage_instruction_1_operation, multiplexer_1_out;
  wire [7:0] decodage_instruction_1_b_data_for_registre_result, decodage_instruction_1_e_addr_ram,
       multiplexer_2_out, pointeur_programme_1_curr_adress, ram_1_dout;
  wire [15:0] rom_1_data;

  Pointeur_Programme pointeur_programme_1 (
    .WE(WE), .CLOCK(CLOCK), .RESET(RESET_POINTEUR_PROGRAMME), .CURR_ADRESS(pointeur_programme_1_curr_adress));
  ROM #(.dataWidth(16)) rom_1 (.addr(pointeur_programme_1_curr_adress), .data(rom_1_data));
  DECODAGE_INSTRUCTION decodage_instruction_1 (
    .INSTRUCTION_ROM(rom_1_data), .WE(decodage_instruction_1_we),
    .c_ADDR_REGISTRE_OPERANDE2(decodage_instruction_1_c_addr_registre_operande2),
    .b_ADDR_REGISTRE_OPERANDE1(decodage_instruction_1_b_addr_registre_operande1),
    .a_DATA_TO_STOCK_RAM(out_7), .e_ADDR_RAM(decodage_instruction_1_e_addr_ram),
    .b_DATA_FOR_REGISTRE_RESULT(decodage_instruction_1_b_data_for_registre_result),
    .a_ADDR_REGISTRE_RESULT(decodage_instruction_1_a_addr_registre_result),
    .d_ADDR_REGISTRE_SRC_STOCK(decodage_instruction_1_d_addr_registre_src_stock),
    .OPERATION(decodage_instruction_1_operation),
    .REGISTRE_OPERATION_DATA(decodage_instruction_1_registre_operation_data),
    .RAM_WRITE(decodage_instruction_1_ram_write), .LOAD_IMMEDIAT(decodage_instruction_1_load_immediat),
    .RAM_READ(decodage_instruction_1_ram_read), .LOAD_RAM(decodage_instruction_1_load_ram));
  Multiplexer #(.width(2)) multiplexer_1 (
    .in0(decodage_instruction_1_b_addr_registre_operande1),
    .in1(decodage_instruction_1_d_addr_registre_src_stock), .out(multiplexer_1_out),
    .sel(decodage_instruction_1_load_ram));
  RAM ram_1 (
    .addr(decodage_instruction_1_e_addr_ram), .we(decodage_instruction_1_ram_write),
    .oe(decodage_instruction_1_ram_read), .clk(CLOCK), .din(out_7), .dout(ram_1_dout));
  Multiplexer #(.width(8)) multiplexer_2 (
    .in0(decodage_instruction_1_b_data_for_registre_result), .in1(ram_1_dout), .out(multiplexer_2_out),
    .sel(decodage_instruction_1_load_immediat));
  UAL_ET_BANC ual_et_banc_1 (
    .STORING_REGISTER(decodage_instruction_1_a_addr_registre_result), .WE(decodage_instruction_1_we),
    .RESTE(1'b0), .CLOCK(CLOCK), .OPERATION(decodage_instruction_1_operation), .LOAD_A_IN(multiplexer_1_out),
    .RESET(RESET_REGISTRES), .LOAD_B_IN(decodage_instruction_1_c_addr_registre_operande2),
    .DATA(multiplexer_2_out), .WRITE_RESULT0_OR_DATA1(decodage_instruction_1_registre_operation_data),
    .A(OPERANDE1), .B(OPERANDE2));

  // Notes on the sheet:
  //   contents of rom_1 (hex, n*v repeats v):
  //   4416 8812 c4a cc20 304a
endmodule

module DECODAGE_INSTRUCTION (
  input  [15:0] INSTRUCTION_ROM,
  output WE,
  output [1:0] c_ADDR_REGISTRE_OPERANDE2,
  output [1:0] b_ADDR_REGISTRE_OPERANDE1,
  output [7:0] a_DATA_TO_STOCK_RAM,
  output [7:0] e_ADDR_RAM,
  output [7:0] b_DATA_FOR_REGISTRE_RESULT,
  output [1:0] a_ADDR_REGISTRE_RESULT,
  output [1:0] d_ADDR_REGISTRE_SRC_STOCK,
  output [1:0] OPERATION,
  output REGISTRE_OPERATION_DATA,
  output RAM_WRITE,
  output LOAD_IMMEDIAT,
  output RAM_READ,
  output LOAD_RAM
);

  wire and_3_out, not_1_out, not_2_out, not_3_out;

  not not_1 (not_1_out, INSTRUCTION_ROM[14]);
  not not_2 (not_2_out, INSTRUCTION_ROM[15]);
  and and_1 (REGISTRE_OPERATION_DATA, not_1_out, not_2_out);
  and and_2 (RAM_WRITE, INSTRUCTION_ROM[14], INSTRUCTION_ROM[15]);
  not not_3 (not_3_out, RAM_WRITE);
  and and_3 (and_3_out, not_3_out, 1'b1);
  and and_4 (LOAD_IMMEDIAT, and_3_out, INSTRUCTION_ROM[14]);
  and and_5 (LOAD_RAM, and_3_out, INSTRUCTION_ROM[15]);

  assign a_ADDR_REGISTRE_RESULT = INSTRUCTION_ROM[11:10];
  assign a_DATA_TO_STOCK_RAM = INSTRUCTION_ROM[9:2];
  assign b_ADDR_REGISTRE_OPERANDE1 = INSTRUCTION_ROM[7:6];
  assign b_DATA_FOR_REGISTRE_RESULT = INSTRUCTION_ROM[9:2];
  assign c_ADDR_REGISTRE_OPERANDE2 = INSTRUCTION_ROM[3:2];
  assign d_ADDR_REGISTRE_SRC_STOCK = INSTRUCTION_ROM[11:10];
  assign e_ADDR_RAM = INSTRUCTION_ROM[9:2];
  assign OPERATION = INSTRUCTION_ROM[13:12];
  assign RAM_READ = LOAD_RAM;
  assign WE = INSTRUCTION_ROM[1];
endmodule

module ETAPE9_JUMP (
  input  CLOCK,
  input  RESET_REGISTRES,
  input  RESET_POINTEUR_PROGRAMME,
  output [7:0] OPERANDE1,
  output [7:0] OPERANDE2
);

  wire and_1_out, and_2_out, and_3_out, decodage_instruction_jump_1_jmp,
       decodage_instruction_jump_1_load_immediat, decodage_instruction_jump_1_load_ram,
       decodage_instruction_jump_1_ram_read, decodage_instruction_jump_1_ram_write,
       decodage_instruction_jump_1_registre_operation_data, decodage_instruction_jump_1_we, not_1_out,
       not_2_out;
  wire [1:0] decodage_instruction_jump_1_a_addr_registre_result,
       decodage_instruction_jump_1_b_addr_registre_operande1,
       decodage_instruction_jump_1_c_addr_registre_operande2,
       decodage_instruction_jump_1_d_addr_registre_src_stock, decodage_instruction_jump_1_operation,
       multiplexer_1_out;
  wire [7:0] decodage_instruction_jump_1_a_data_to_stock_ram,
       decodage_instruction_jump_1_b_data_for_registre_result, decodage_instruction_jump_1_e_addr_ram,
       decodage_instruction_jump_1_jmp_addr, multiplexer_2_out, pointeur_programme_jmp_1_curr_adress,
       ram_1_dout;
  wire [15:0] rom_1_data;

  POINTEUR_PROGRAMME_JMP pointeur_programme_jmp_1 (
    .JMP_ADDRR(decodage_instruction_jump_1_jmp_addr), .CLOCK(CLOCK), .JMP(decodage_instruction_jump_1_jmp),
    .RESET(RESET_POINTEUR_PROGRAMME), .CURR_ADRESS(pointeur_programme_jmp_1_curr_adress));
  ROM #(.dataWidth(16)) rom_1 (.addr(pointeur_programme_jmp_1_curr_adress), .data(rom_1_data));
  DECODAGE_INSTRUCTION_JUMP decodage_instruction_jump_1 (
    .INSTRUCTION_ROM(rom_1_data), .JMP(decodage_instruction_jump_1_jmp), .WE(decodage_instruction_jump_1_we),
    .c_ADDR_REGISTRE_OPERANDE2(decodage_instruction_jump_1_c_addr_registre_operande2),
    .b_ADDR_REGISTRE_OPERANDE1(decodage_instruction_jump_1_b_addr_registre_operande1),
    .a_DATA_TO_STOCK_RAM(decodage_instruction_jump_1_a_data_to_stock_ram),
    .e_ADDR_RAM(decodage_instruction_jump_1_e_addr_ram),
    .b_DATA_FOR_REGISTRE_RESULT(decodage_instruction_jump_1_b_data_for_registre_result),
    .a_ADDR_REGISTRE_RESULT(decodage_instruction_jump_1_a_addr_registre_result),
    .JMP_ADDR(decodage_instruction_jump_1_jmp_addr),
    .d_ADDR_REGISTRE_SRC_STOCK(decodage_instruction_jump_1_d_addr_registre_src_stock),
    .OPERATION(decodage_instruction_jump_1_operation),
    .REGISTRE_OPERATION_DATA(decodage_instruction_jump_1_registre_operation_data),
    .RAM_WRITE(decodage_instruction_jump_1_ram_write),
    .LOAD_IMMEDIAT(decodage_instruction_jump_1_load_immediat),
    .RAM_READ(decodage_instruction_jump_1_ram_read), .LOAD_RAM(decodage_instruction_jump_1_load_ram));
  Multiplexer #(.width(2)) multiplexer_1 (
    .in0(decodage_instruction_jump_1_b_addr_registre_operande1),
    .in1(decodage_instruction_jump_1_d_addr_registre_src_stock), .out(multiplexer_1_out),
    .sel(decodage_instruction_jump_1_load_ram));
  not not_1 (not_1_out, decodage_instruction_jump_1_jmp);
  not not_2 (not_2_out, decodage_instruction_jump_1_jmp);
  and and_1 (and_1_out, not_2_out, decodage_instruction_jump_1_we);
  Multiplexer #(.width(8)) multiplexer_2 (
    .in0(decodage_instruction_jump_1_b_data_for_registre_result), .in1(ram_1_dout), .out(multiplexer_2_out),
    .sel(decodage_instruction_jump_1_load_immediat));
  and and_2 (and_2_out, decodage_instruction_jump_1_ram_write, not_1_out);
  RAM ram_1 (
    .addr(decodage_instruction_jump_1_e_addr_ram), .we(and_2_out), .oe(and_3_out), .clk(CLOCK),
    .din(decodage_instruction_jump_1_a_data_to_stock_ram), .dout(ram_1_dout));
  and and_3 (and_3_out, decodage_instruction_jump_1_ram_read, not_1_out);
  UAL_ET_BANC ual_et_banc_1 (
    .STORING_REGISTER(decodage_instruction_jump_1_a_addr_registre_result), .WE(and_1_out), .RESTE(1'b0),
    .CLOCK(CLOCK), .OPERATION(decodage_instruction_jump_1_operation), .LOAD_A_IN(multiplexer_1_out),
    .RESET(RESET_REGISTRES), .LOAD_B_IN(decodage_instruction_jump_1_c_addr_registre_operande2),
    .DATA(multiplexer_2_out), .WRITE_RESULT0_OR_DATA1(decodage_instruction_jump_1_registre_operation_data),
    .A(OPERANDE1), .B(OPERANDE2));

  // Notes on the sheet:
  //   contents of rom_1 (hex, n*v repeats v):
  //   4416 8812 c4a cc20 304a
endmodule

module DECODAGE_INSTRUCTION_JUMP (
  input  [15:0] INSTRUCTION_ROM,
  output JMP,
  output WE,
  output [1:0] c_ADDR_REGISTRE_OPERANDE2,
  output [1:0] b_ADDR_REGISTRE_OPERANDE1,
  output [7:0] a_DATA_TO_STOCK_RAM,
  output [7:0] e_ADDR_RAM,
  output [7:0] b_DATA_FOR_REGISTRE_RESULT,
  output [1:0] a_ADDR_REGISTRE_RESULT,
  output [7:0] JMP_ADDR,
  output [1:0] d_ADDR_REGISTRE_SRC_STOCK,
  output [1:0] OPERATION,
  output REGISTRE_OPERATION_DATA,
  output RAM_WRITE,
  output LOAD_IMMEDIAT,
  output RAM_READ,
  output LOAD_RAM
);

  wire and_3_out, not_1_out, not_2_out, not_3_out;

  not not_1 (not_1_out, INSTRUCTION_ROM[14]);
  not not_2 (not_2_out, INSTRUCTION_ROM[15]);
  and and_1 (REGISTRE_OPERATION_DATA, not_1_out, not_2_out);
  and and_2 (RAM_WRITE, INSTRUCTION_ROM[14], INSTRUCTION_ROM[15]);
  not not_3 (not_3_out, RAM_WRITE);
  and and_3 (and_3_out, not_3_out, 1'b1);
  and and_4 (LOAD_IMMEDIAT, and_3_out, INSTRUCTION_ROM[14]);
  and and_5 (LOAD_RAM, and_3_out, INSTRUCTION_ROM[15]);

  assign a_ADDR_REGISTRE_RESULT = INSTRUCTION_ROM[11:10];
  assign a_DATA_TO_STOCK_RAM = INSTRUCTION_ROM[9:2];
  assign b_ADDR_REGISTRE_OPERANDE1 = INSTRUCTION_ROM[7:6];
  assign b_DATA_FOR_REGISTRE_RESULT = INSTRUCTION_ROM[9:2];
  assign c_ADDR_REGISTRE_OPERANDE2 = INSTRUCTION_ROM[3:2];
  assign d_ADDR_REGISTRE_SRC_STOCK = INSTRUCTION_ROM[11:10];
  assign e_ADDR_RAM = INSTRUCTION_ROM[9:2];
  assign JMP = INSTRUCTION_ROM[0];
  assign JMP_ADDR = INSTRUCTION_ROM[9:2];
  assign OPERATION = INSTRUCTION_ROM[13:12];
  assign RAM_READ = LOAD_RAM;
  assign WE = INSTRUCTION_ROM[1];
endmodule

module POINTEUR_PROGRAMME_JMP (
  input  [7:0] JMP_ADDRR,
  input  CLOCK,
  input  JMP,
  input  RESET,
  output [7:0] CURR_ADRESS
);

  wire additioneur_8_bits_1_retenue_out;
  wire [7:0] additioneur_8_bits_1_somme, multiplexer_1_out;

  ADDITIONEUR_8_bits additioneur_8_bits_1 (
    .A(CURR_ADRESS), .B(8'h1), .RESTE(additioneur_8_bits_1_retenue_out), .Somme(additioneur_8_bits_1_somme),
    .RETENUE_OUT(additioneur_8_bits_1_retenue_out));
  Multiplexer #(.width(8)) multiplexer_1 (
    .in0(additioneur_8_bits_1_somme), .in1(JMP_ADDRR), .out(multiplexer_1_out), .sel(JMP));
  REGISTRE_8_bits registre_8_bits_1 (
    .DONNEES(multiplexer_1_out), .WE(1'b1), .CLOCK(CLOCK), .RESET(RESET), .FORMER_DATA(CURR_ADRESS));
endmodule
